# Fritzing sketch blink sem delay (saved by Fritzing 0.9.6b)
breadboards: 1

parts:
  Part1 = Arduino Mega 2560 (Rev3)
  R1 = Resistor [tolerance=±5% resistance=220 package="0402 [SMD]"]
  LED2 = LED - 3mm [color="Red (633nm)" current=0.030 package="3 mm [THT]"]

nets:
  N1: Part1.GND, R1.Pin_0
  N2: Part1.D13_PWM, LED2.anode
  N3: R1.Pin_1, LED2.cathode

notes:
  Observe a polaridade do LED.
