# Fritzing sketch blinkSemDelay (saved by Fritzing 0.9.6b)
breadboards: 1

parts:
  Part1 = Arduino Mega 2560 (Rev3)
  LED2 = LED - 3mm [color="Red (633nm)" current=0.030 package="3 mm [THT]"]
  R1 = Resistor [tolerance=±5% power=0.25 resistance=220 package=THT]

nets:
  N1: Part1.GND, R1.Pin_0
  N2: Part1.D13_PWM, LED2.anode
  N3: LED2.cathode, R1.Pin_1

notes:
  Observe a polaridade do LED.
